// Logisim project relojDigital.circ as structural Verilog: 6 circuits, main circuit main
module main (
);

  wire Activador_Alarma_out, and_1_out, and_2_out, and_3_out, button_1_out, button_2_out, button_3_out,
       button_4_out, circuito0a5_1_carryout, circuito0a5_2_carryout, contador0a9_1_carryout,
       contador0a9_2_carryout, contador0a9_3_carryout, decobcd1_1_a, decobcd1_1_b, decobcd1_1_c,
       decobcd1_1_d, decobcd1_1_e, decobcd1_1_f, decobcd1_1_g, decobcd1_2_a, decobcd1_2_b, decobcd1_2_c,
       decobcd1_2_d, decobcd1_2_e, decobcd1_2_f, decobcd1_2_g, decobcd1_3_a, decobcd1_3_b, decobcd1_3_c,
       decobcd1_3_d, decobcd1_3_e, decobcd1_3_f, decobcd1_3_g, decobcd1_4_a, decobcd1_4_b, decobcd1_4_c,
       decobcd1_4_d, decobcd1_4_e, decobcd1_4_f, decobcd1_4_g, decobcd1_5_a, decobcd1_5_b, decobcd1_5_c,
       decobcd1_5_d, decobcd1_5_e, decobcd1_5_f, decobcd1_5_g, decobcd1_6_a, decobcd1_6_b, decobcd1_6_c,
       decobcd1_6_d, decobcd1_6_e, decobcd1_6_f, decobcd1_6_g, decobcd1_7_a, decobcd1_7_b, decobcd1_7_c,
       decobcd1_7_d, decobcd1_7_e, decobcd1_7_f, decobcd1_7_g, decobcd1_8_a, decobcd1_8_b, decobcd1_8_c,
       decobcd1_8_d, decobcd1_8_e, decobcd1_8_f, decobcd1_8_g, decobcd1_9_a, decobcd1_9_b, decobcd1_9_c,
       decobcd1_9_d, decobcd1_9_e, decobcd1_9_f, decobcd1_9_g, decobcd1_10_a, decobcd1_10_b, decobcd1_10_c,
       decobcd1_10_d, decobcd1_10_e, decobcd1_10_f, decobcd1_10_g, not_1_out, not_2_out, not_3_out,
       not_4_out, reset24hrs_out, reset_alarm_out, RESET_out, rgbled_2_p1, rgbled_2_p2, rgbled_4_p1;
  wire [3:0] alarma_1_dec_hor, alarma_1_decen_min, alarma_1_unid_hora, alarma_1_unid_min, and_4_out,
       and_5_out, and_6_out, circuito0a5_1_q0, circuito0a5_2_q0, contador0a2_1_q0, contador0a9_1_q0,
       contador0a9_2_q0, contador0a9_3_q0, not_5_out, not_6_out, not_7_out, not_8_out, xor_1_out, xor_2_out,
       xor_3_out, xor_4_out;

  DecoBCD1 decobcd1_1 (
    .BCD(contador0a2_1_q0), .A(decobcd1_1_a), .B(decobcd1_1_b), .C(decobcd1_1_c), .D(decobcd1_1_d),
    .E(decobcd1_1_e), .F(decobcd1_1_f), .G(decobcd1_1_g));
  not not_1 (not_1_out, contador0a2_1_q0[0]);
  and and_1 (and_1_out, not_1_out, contador0a2_1_q0[1]);
  _7_Segment_Display u_7_segment_display_1 (
    .g(decobcd1_1_g), .f(decobcd1_1_f), .a(decobcd1_1_a), .b(decobcd1_1_b), .e(decobcd1_1_e),
    .d(decobcd1_1_d), .c(decobcd1_1_c));  // open: dp
  contador0a2 contador0a2_1 (
    .CLK(contador0a9_1_carryout), .RESET(reset24hrs_out), .V0(contador0a2_1_q0[3]),
    .V00(contador0a2_1_q0[2]), .Q1(contador0a2_1_q0[1]), .Q0(contador0a2_1_q0[0]));  // open: carryout
  and and_2 (and_2_out, and_1_out, and_3_out);
  _7_Segment_Display u_7_segment_display_2 (
    .g(decobcd1_2_g), .f(decobcd1_2_f), .a(decobcd1_2_a), .b(decobcd1_2_b), .e(decobcd1_2_e),
    .d(decobcd1_2_d), .c(decobcd1_2_c));  // open: dp
  DecoBCD1 decobcd1_2 (
    .BCD(contador0a9_1_q0), .A(decobcd1_2_a), .B(decobcd1_2_b), .C(decobcd1_2_c), .D(decobcd1_2_d),
    .E(decobcd1_2_e), .F(decobcd1_2_f), .G(decobcd1_2_g));
  Contador0a9 contador0a9_1 (
    .CLIK(circuito0a5_1_carryout), .RESET(reset24hrs_out), .Q3(contador0a9_1_q0[3]),
    .Q2(contador0a9_1_q0[2]), .Q1(contador0a9_1_q0[1]), .Q0(contador0a9_1_q0[0]),
    .cARRYOUT(contador0a9_1_carryout));
  not not_2 (not_2_out, contador0a9_1_q0[1]);
  not not_3 (not_3_out, contador0a9_1_q0[3]);
  and and_3 (and_3_out, not_3_out, contador0a9_1_q0[2], not_2_out, not_4_out);
  not not_4 (not_4_out, contador0a9_1_q0[0]);
  // RGBLED rgbled_1: pin names not known
  // RGBLED rgbled_2: pin names not known; wires that end beside it: rgbled_2_p1, rgbled_2_p2, rgbled_2_p1
  DecoBCD1 decobcd1_3 (
    .BCD(circuito0a5_1_q0), .A(decobcd1_3_a), .B(decobcd1_3_b), .C(decobcd1_3_c), .D(decobcd1_3_d),
    .E(decobcd1_3_e), .F(decobcd1_3_f), .G(decobcd1_3_g));
  circuito0a5 circuito0a5_1 (
    .CLK(contador0a9_2_carryout), .Reset(RESET_out), .v0(circuito0a5_1_q0[3]), .Q2(circuito0a5_1_q0[2]),
    .Q1(circuito0a5_1_q0[1]), .Q0(circuito0a5_1_q0[0]), .CARRYOUT(circuito0a5_1_carryout));
  or reset24hrs (reset24hrs_out, RESET_out, and_2_out);
  _7_Segment_Display u_7_segment_display_3 (
    .g(decobcd1_3_g), .f(decobcd1_3_f), .a(decobcd1_3_a), .b(decobcd1_3_b), .e(decobcd1_3_e),
    .d(decobcd1_3_d), .c(decobcd1_3_c));  // open: dp
  DecoBCD1 decobcd1_4 (
    .BCD(contador0a9_2_q0), .A(decobcd1_4_a), .B(decobcd1_4_b), .C(decobcd1_4_c), .D(decobcd1_4_d),
    .E(decobcd1_4_e), .F(decobcd1_4_f), .G(decobcd1_4_g));
  Contador0a9 contador0a9_2 (
    .CLIK(circuito0a5_2_carryout), .RESET(RESET_out), .Q3(contador0a9_2_q0[3]), .Q2(contador0a9_2_q0[2]),
    .Q1(contador0a9_2_q0[1]), .Q0(contador0a9_2_q0[0]), .cARRYOUT(contador0a9_2_carryout));
  _7_Segment_Display u_7_segment_display_4 (
    .g(decobcd1_4_g), .f(decobcd1_4_f), .a(decobcd1_4_a), .b(decobcd1_4_b), .e(decobcd1_4_e),
    .d(decobcd1_4_d), .c(decobcd1_4_c));  // open: dp
  // RGBLED rgbled_3: pin names not known
  // RGBLED rgbled_4: pin names not known; wires that end beside it: rgbled_4_p1, rgbled_2_p2, rgbled_4_p1
  _7_Segment_Display u_7_segment_display_5 (
    .g(decobcd1_5_g), .f(decobcd1_5_f), .a(decobcd1_5_a), .b(decobcd1_5_b), .e(decobcd1_5_e),
    .d(decobcd1_5_d), .c(decobcd1_5_c));  // open: dp
  DecoBCD1 decobcd1_5 (
    .BCD(circuito0a5_2_q0), .A(decobcd1_5_a), .B(decobcd1_5_b), .C(decobcd1_5_c), .D(decobcd1_5_d),
    .E(decobcd1_5_e), .F(decobcd1_5_f), .G(decobcd1_5_g));
  circuito0a5 circuito0a5_2 (
    .CLK(contador0a9_3_carryout), .Reset(RESET_out), .v0(circuito0a5_2_q0[3]), .Q2(circuito0a5_2_q0[2]),
    .Q1(circuito0a5_2_q0[1]), .Q0(circuito0a5_2_q0[0]), .CARRYOUT(circuito0a5_2_carryout));
  assign xor_1_out = contador0a2_1_q0 ^ alarma_1_dec_hor;  // XOR_Gate xor_1, 4 bits wide
  assign not_5_out = ~xor_1_out;  // NOT_Gate not_5, 4 bits wide
  assign xor_2_out = contador0a9_1_q0 ^ alarma_1_unid_hora;  // XOR_Gate xor_2, 4 bits wide
  assign not_6_out = ~xor_2_out;  // NOT_Gate not_6, 4 bits wide
  assign and_4_out = not_5_out & not_6_out;  // AND_Gate and_4, 4 bits wide
  DecoBCD1 decobcd1_6 (
    .BCD(contador0a9_3_q0), .A(decobcd1_6_a), .B(decobcd1_6_b), .C(decobcd1_6_c), .D(decobcd1_6_d),
    .E(decobcd1_6_e), .F(decobcd1_6_f), .G(decobcd1_6_g));
  Contador0a9 contador0a9_3 (
    .CLIK(rgbled_2_p2), .RESET(RESET_out), .Q3(contador0a9_3_q0[3]), .Q2(contador0a9_3_q0[2]),
    .Q1(contador0a9_3_q0[1]), .Q0(contador0a9_3_q0[0]), .cARRYOUT(contador0a9_3_carryout));
  assign xor_3_out = circuito0a5_1_q0 ^ alarma_1_decen_min;  // XOR_Gate xor_3, 4 bits wide
  assign not_7_out = ~xor_3_out;  // NOT_Gate not_7, 4 bits wide
  assign and_5_out = and_4_out & and_6_out;  // AND_Gate and_5, 4 bits wide
  _7_Segment_Display u_7_segment_display_6 (
    .g(decobcd1_6_g), .f(decobcd1_6_f), .a(decobcd1_6_a), .b(decobcd1_6_b), .e(decobcd1_6_e),
    .d(decobcd1_6_d), .c(decobcd1_6_c));  // open: dp
  assign xor_4_out = contador0a9_2_q0 ^ alarma_1_unid_min;  // XOR_Gate xor_4, 4 bits wide
  assign not_8_out = ~xor_4_out;  // NOT_Gate not_8, 4 bits wide
  assign and_6_out = not_7_out & not_8_out;  // AND_Gate and_6, 4 bits wide
  and Activador_Alarma (Activador_Alarma_out, and_5_out[0], and_5_out[1], and_5_out[2], and_5_out[3]);
  Button RESET (.out(RESET_out));
  Clock CLK (.out(rgbled_2_p2));
  LED led_1 (.in(Activador_Alarma_out));
  LED led_2 (.in(Activador_Alarma_out));
  LED led_3 (.in(Activador_Alarma_out));
  LED led_4 (.in(Activador_Alarma_out));
  LED led_5 (.in(Activador_Alarma_out));
  LED led_6 (.in(Activador_Alarma_out));
  LED led_7 (.in(Activador_Alarma_out));
  LED led_8 (.in(Activador_Alarma_out));
  DecoBCD1 decobcd1_7 (
    .BCD(alarma_1_dec_hor), .A(decobcd1_7_a), .B(decobcd1_7_b), .C(decobcd1_7_c), .D(decobcd1_7_d),
    .E(decobcd1_7_e), .F(decobcd1_7_f), .G(decobcd1_7_g));
  _7_Segment_Display u_7_segment_display_7 (
    .g(decobcd1_7_g), .f(decobcd1_7_f), .a(decobcd1_7_a), .b(decobcd1_7_b), .e(decobcd1_7_e),
    .d(decobcd1_7_d), .c(decobcd1_7_c));  // open: dp
  DecoBCD1 decobcd1_8 (
    .BCD(alarma_1_unid_hora), .A(decobcd1_8_a), .B(decobcd1_8_b), .C(decobcd1_8_c), .D(decobcd1_8_d),
    .E(decobcd1_8_e), .F(decobcd1_8_f), .G(decobcd1_8_g));
  Alarma alarma_1 (
    .in_1(button_1_out), .in_2(reset_alarm_out), .in_3(button_2_out), .in_4(button_3_out),
    .in_5(button_4_out), .dec_hor(alarma_1_dec_hor), .Unid_hora(alarma_1_unid_hora),
    .decen_min(alarma_1_decen_min), .unid_min(alarma_1_unid_min));
  Button button_1 (.out(button_1_out));
  Button button_2 (.out(button_2_out));
  Button reset_alarm (.out(reset_alarm_out));
  _7_Segment_Display u_7_segment_display_8 (
    .g(decobcd1_8_g), .f(decobcd1_8_f), .a(decobcd1_8_a), .b(decobcd1_8_b), .e(decobcd1_8_e),
    .d(decobcd1_8_d), .c(decobcd1_8_c));  // open: dp
  Button button_3 (.out(button_3_out));
  Button button_4 (.out(button_4_out));
  LED led_9 (.in(rgbled_2_p2));
  LED led_10 (.in(rgbled_2_p2));
  DecoBCD1 decobcd1_9 (
    .BCD(alarma_1_decen_min), .A(decobcd1_9_a), .B(decobcd1_9_b), .C(decobcd1_9_c), .D(decobcd1_9_d),
    .E(decobcd1_9_e), .F(decobcd1_9_f), .G(decobcd1_9_g));
  _7_Segment_Display u_7_segment_display_9 (
    .g(decobcd1_9_g), .f(decobcd1_9_f), .a(decobcd1_9_a), .b(decobcd1_9_b), .e(decobcd1_9_e),
    .d(decobcd1_9_d), .c(decobcd1_9_c));  // open: dp
  DecoBCD1 decobcd1_10 (
    .BCD(alarma_1_unid_min), .A(decobcd1_10_a), .B(decobcd1_10_b), .C(decobcd1_10_c), .D(decobcd1_10_d),
    .E(decobcd1_10_e), .F(decobcd1_10_f), .G(decobcd1_10_g));
  _7_Segment_Display u_7_segment_display_10 (
    .g(decobcd1_10_g), .f(decobcd1_10_f), .a(decobcd1_10_a), .b(decobcd1_10_b), .e(decobcd1_10_e),
    .d(decobcd1_10_d), .c(decobcd1_10_c));  // open: dp
  LED led_11 (.in(Activador_Alarma_out));
  LED led_12 (.in(Activador_Alarma_out));
  LED led_13 (.in(Activador_Alarma_out));
  LED led_14 (.in(Activador_Alarma_out));
  LED led_15 (.in(Activador_Alarma_out));
  LED led_16 (.in(Activador_Alarma_out));
  LED led_17 (.in(Activador_Alarma_out));
  LED led_18 (.in(Activador_Alarma_out));
endmodule

module DecoBCD1 (
  input  [3:0] BCD,
  output A,
  output B,
  output C,
  output D,
  output E,
  output F,
  output G
);

  wire and_1_out, and_2_out, and_3_out, and_4_out, and_5_out, and_6_out, and_7_out, and_8_out, and_9_out,
       and_10_out, and_11_out, and_12_out, and_13_out, and_14_out, and_15_out, and_16_out, not_1_out,
       not_2_out, not_3_out;

  not not_1 (not_1_out, BCD[2]);
  not not_2 (not_2_out, BCD[1]);
  not not_3 (not_3_out, BCD[0]);
  and and_1 (and_1_out, not_1_out, not_3_out);
  and and_2 (and_2_out, BCD[2], BCD[0]);
  and and_3 (and_3_out, not_2_out, not_3_out);
  and and_4 (and_4_out, BCD[1], BCD[0]);
  or or_1 (C, not_2_out, BCD[2], BCD[0]);
  and and_5 (and_5_out, not_2_out, BCD[2], BCD[0]);
  and and_6 (and_6_out, BCD[1], not_3_out);
  and and_7 (and_7_out, BCD[1], not_1_out);
  and and_8 (and_8_out, not_1_out, not_3_out);
  and and_9 (and_9_out, not_1_out, not_3_out);
  and and_10 (and_10_out, BCD[1], not_3_out);
  and and_11 (and_11_out, not_2_out, not_3_out);
  and and_12 (and_12_out, BCD[2], not_3_out);
  and and_13 (and_13_out, BCD[2], not_2_out);
  and and_14 (and_14_out, not_2_out, BCD[2]);
  and and_15 (and_15_out, BCD[1], not_3_out);
  and and_16 (and_16_out, BCD[1], not_1_out);
  or or_2 (A, and_1_out, BCD[3], BCD[1], and_2_out);
  or or_3 (B, and_3_out, not_1_out, and_4_out);
  or or_4 (D, and_5_out, BCD[3], and_6_out, and_7_out, and_8_out);
  or or_5 (E, and_9_out, and_10_out);
  or or_6 (F, and_11_out, and_12_out, and_13_out, BCD[3]);
  or or_7 (G, and_14_out, and_15_out, and_16_out, BCD[3]);
endmodule

module Contador0a9 (
  input  CLIK,
  input  RESET,
  output Q3,
  output Q2,
  output Q1,
  output Q0,
  output cARRYOUT
);

  wire and_1_out, and_2_out, and_3_out, and_4_out, not_1_out, not_2_out, not_3_out, not_4_out, not_5_out,
       or_1_out;

  T_Flip_Flop T3 (.T(or_1_out), .clk(CLIK), .Q(Q3), .reset(RESET));  // open: Qn, preset
  or or_1 (or_1_out, and_1_out, and_2_out);
  and and_1 (and_1_out, Q3, Q0);
  and and_2 (and_2_out, Q2, Q1, Q0);
  T_Flip_Flop T2 (.T(and_3_out), .clk(CLIK), .Q(Q2), .reset(RESET));  // open: Qn, preset
  and and_3 (and_3_out, Q1, Q0);
  T_Flip_Flop T1 (.T(and_4_out), .clk(CLIK), .Q(Q1), .reset(RESET));  // open: Qn, preset
  and and_4 (and_4_out, not_1_out, Q0);
  not not_1 (not_1_out, Q3);
  T_Flip_Flop T0 (.T(1'b1), .clk(CLIK), .Q(Q0), .reset(RESET));  // open: Qn, preset
  not not_2 (not_2_out, Q3);
  not not_3 (not_3_out, Q3);
  not not_4 (not_4_out, Q3);
  not not_5 (not_5_out, Q3);
  and and_5 (cARRYOUT, not_2_out, not_3_out, not_4_out, not_5_out);
endmodule

module circuito0a5 (
  input  CLK,
  input  Reset,
  output v0,
  output Q2,
  output Q1,
  output Q0,
  output CARRYOUT
);

  wire A_out, and_1_out, B_out, not_1_out, not_2_out, not_3_out, not_5_out, not_6_out, not_7_out, not_8_out,
       or_1_out;

  T_Flip_Flop T2 (.T(or_1_out), .clk(CLK), .Q(Q2), .reset(Reset));  // open: Qn, preset
  not not_1 (not_1_out, Q2);
  T_Flip_Flop T1 (.T(and_1_out), .clk(CLK), .Q(Q1), .reset(Reset));  // open: Qn, preset
  T_Flip_Flop T0 (.T(1'b1), .clk(CLK), .Q(Q0), .reset(Reset));  // open: Qn, preset
  not not_2 (not_2_out, Q2);
  not not_3 (not_3_out, Q1);
  and and_1 (and_1_out, not_1_out, Q0);
  and A (A_out, not_2_out, Q1, Q0);
  and B (B_out, Q2, not_3_out, Q0);
  or or_1 (or_1_out, A_out, B_out);
  not not_4 (v0, 1'b1);
  not not_5 (not_5_out, v0);
  not not_6 (not_6_out, Q2);
  not not_7 (not_7_out, Q1);
  not not_8 (not_8_out, Q0);
  and and_2 (CARRYOUT, not_5_out, not_6_out, not_7_out, not_8_out);
endmodule

module contador0a2 (
  input  CLK,
  input  RESET,
  output V0,
  output V00,
  output Q1,
  output Q0,
  output carryout
);

  wire not_1_out, not_4_out, not_5_out, not_6_out, not_7_out, or_1_out;

  T_Flip_Flop T1 (.T(or_1_out), .clk(CLK), .Q(Q1), .reset(RESET));  // open: Qn, preset
  not not_1 (not_1_out, Q1);
  T_Flip_Flop T0 (.T(not_1_out), .clk(CLK), .Q(Q0), .reset(RESET));  // open: Qn, preset
  or or_1 (or_1_out, Q1, Q0);
  not not_2 (V0, 1'b1);
  not not_3 (V00, 1'b1);
  not not_4 (not_4_out, V0);
  not not_5 (not_5_out, V0);
  not not_6 (not_6_out, V0);
  not not_7 (not_7_out, V0);
  and and_1 (carryout, not_4_out, not_5_out, not_6_out, not_7_out);
endmodule

module Alarma (
  input  in_1,
  input  in_2,
  input  in_3,
  input  in_4,
  input  in_5,
  output [3:0] dec_hor,
  output [3:0] Unid_hora,
  output [3:0] decen_min,
  output [3:0] unid_min
);

  contador0a2 contador0a2_1 (
    .CLK(in_1), .RESET(in_2), .V0(dec_hor[3]), .V00(dec_hor[2]), .Q1(dec_hor[1]), .Q0(dec_hor[0]));  // open: carryout
  Contador0a9 contador0a9_1 (
    .CLIK(in_3), .RESET(in_2), .Q3(Unid_hora[3]), .Q2(Unid_hora[2]), .Q1(Unid_hora[1]), .Q0(Unid_hora[0]));  // open: cARRYOUT
  circuito0a5 circuito0a5_1 (
    .CLK(in_4), .Reset(in_2), .v0(decen_min[3]), .Q2(decen_min[2]), .Q1(decen_min[1]), .Q0(decen_min[0]));  // open: CARRYOUT
  Contador0a9 contador0a9_2 (
    .CLIK(in_5), .RESET(in_2), .Q3(unid_min[3]), .Q2(unid_min[2]), .Q1(unid_min[1]), .Q0(unid_min[0]));  // open: cARRYOUT
endmodule
